# Fritzing sketch aircon_wiring (saved by Fritzing 0.9.3b)
breadboards: 1

parts:
  U1 = ESP32-38PinWide [part_number=ESP32-38PinWide]
  J1 = Basic Servo
  DHT1 = Humidity and Temperature Sensor DHT11

nets:
  N1: U1.GPIO33, DHT1.Data-signal
  GND: U1.GND, J1.gnd, DHT1.GND_1
  VCC: U1.VIN, J1.vcc, DHT1.Vcc

custom parts:
  ESP32-38PinWide: Generic 38-Pin ESP32 with wide format (only access to one side of pins on a breadboard) based on Stephen Lilley's HiLetgo ESP-WROOM-32 ESP32 ESP-32S Development Board.
  Humidity and Temperature Sensor DHT11: Digital relative humidity & temperature sensor DHT11
